# Fritzing sketch BebyMatris (saved by Fritzing 0.8.3b)
stripboards: 10

parts:
  Parte2 = Lilypad Arduino Board
  Parte103 = LilyPad Tri-Color LED
  Parte104 = LilyPad Tri-Color LED
  Parte105 = LilyPad Tri-Color LED
  Parte106 = LilyPad Tri-Color LED
  Parte107 = LilyPad Tri-Color LED
  Parte108 = LilyPad Tri-Color LED
  Parte109 = LilyPad Tri-Color LED
  Parte110 = LilyPad Tri-Color LED
  Parte111 = LilyPad Tri-Color LED
  Parte112 = LilyPad Tri-Color LED
  Parte113 = LilyPad Tri-Color LED
  Parte114 = LilyPad Tri-Color LED
  Parte115 = LilyPad Tri-Color LED
  Parte116 = LilyPad Tri-Color LED
  Parte117 = LilyPad Tri-Color LED
  Parte118 = LilyPad Tri-Color LED
  Parte119 = LilyPad Tri-Color LED
  Parte120 = LilyPad Tri-Color LED
  Parte121 = LilyPad Tri-Color LED
  Parte122 = LilyPad Tri-Color LED
  Parte123 = LilyPad Tri-Color LED
  Parte124 = LilyPad Tri-Color LED
  Parte125 = LilyPad Tri-Color LED
  Parte126 = LilyPad Tri-Color LED
  Parte127 = LilyPad Tri-Color LED
  Parte128 = LilyPad Tri-Color LED
  Parte129 = LilyPad Tri-Color LED
  Parte130 = LilyPad Tri-Color LED
  Parte131 = LilyPad Tri-Color LED
  Parte132 = LilyPad Tri-Color LED
  Parte133 = LilyPad Tri-Color LED
  Parte134 = LilyPad Tri-Color LED
  Parte135 = LilyPad Tri-Color LED
  Parte136 = LilyPad Tri-Color LED
  Parte137 = LilyPad Tri-Color LED
  Parte138 = LilyPad Tri-Color LED
  Parte139 = LilyPad Tri-Color LED
  Parte140 = LilyPad Tri-Color LED
  Parte141 = LilyPad Tri-Color LED
  Parte142 = LilyPad Tri-Color LED
  Parte143 = LilyPad Tri-Color LED
  Parte144 = LilyPad Tri-Color LED
  Parte145 = LilyPad Tri-Color LED
  Parte146 = LilyPad Tri-Color LED
  Parte147 = LilyPad Tri-Color LED
  Parte148 = LilyPad Tri-Color LED
  Parte149 = LilyPad Tri-Color LED
  Parte150 = LilyPad Tri-Color LED
  Parte151 = LilyPad Tri-Color LED
  Parte152 = LilyPad Tri-Color LED
  Parte153 = LilyPad Tri-Color LED
  Parte154 = LilyPad Tri-Color LED
  Parte155 = LilyPad Tri-Color LED
  Parte156 = LilyPad Tri-Color LED
  Parte157 = LilyPad Tri-Color LED
  Parte158 = LilyPad Tri-Color LED
  Parte159 = LilyPad Tri-Color LED
  Parte160 = LilyPad Tri-Color LED
  Parte161 = LilyPad Tri-Color LED
  Parte162 = LilyPad Tri-Color LED
  Parte163 = LilyPad Tri-Color LED
  Parte164 = LilyPad Tri-Color LED
  Parte165 = LilyPad Tri-Color LED
  Parte166 = LilyPad Tri-Color LED
  Parte167 = LilyPad Tri-Color LED
  Parte168 = LilyPad Tri-Color LED
  Parte169 = LilyPad Tri-Color LED
  Parte170 = LilyPad Tri-Color LED
  Parte171 = LilyPad Tri-Color LED
  Parte172 = LilyPad Tri-Color LED
  Parte173 = LilyPad Tri-Color LED
  Parte174 = LilyPad Tri-Color LED
  Parte175 = LilyPad Tri-Color LED
  Parte176 = LilyPad Tri-Color LED
  Parte177 = LilyPad Tri-Color LED
  Parte178 = LilyPad Tri-Color LED
  Parte179 = LilyPad Tri-Color LED
  Parte180 = LilyPad Tri-Color LED
  Parte181 = LilyPad Tri-Color LED
  Parte182 = LilyPad Tri-Color LED
  Parte183 = LilyPad Tri-Color LED
  Parte184 = LilyPad Tri-Color LED
  Parte185 = LilyPad Tri-Color LED
  Parte186 = LilyPad Tri-Color LED
  Parte187 = LilyPad Tri-Color LED
  Parte188 = LilyPad Tri-Color LED
  Parte189 = LilyPad Tri-Color LED
  Parte190 = LilyPad Tri-Color LED
  Parte191 = LilyPad Tri-Color LED
  Parte192 = LilyPad Tri-Color LED
  Parte193 = LilyPad Tri-Color LED
  Parte194 = LilyPad Tri-Color LED
  Parte195 = LilyPad Tri-Color LED
  Parte196 = LilyPad Tri-Color LED
  Parte197 = LilyPad Tri-Color LED
  Parte198 = LilyPad Tri-Color LED
  Parte199 = LilyPad Tri-Color LED
  Parte200 = LilyPad Tri-Color LED
  Parte201 = LilyPad Tri-Color LED
  Parte202 = LilyPad Tri-Color LED
  Parte203 = LilyPad LiPower
  Parte204 = LilyPad XBee

nets:
  GND: Parte2.GND, Parte103.Gnd, Parte104.Gnd, Parte105.Gnd, Parte106.Gnd, Parte107.Gnd, Parte108.Gnd, Parte109.Gnd, Parte110.Gnd, Parte111.Gnd, Parte112.Gnd, Parte113.Gnd, Parte114.Gnd, Parte115.Gnd, Parte116.Gnd, Parte117.Gnd, Parte118.Gnd, Parte119.Gnd, Parte120.Gnd, Parte121.Gnd, Parte122.Gnd, Parte203.GND, Parte204.GND
  N1: Parte2.A0, Parte198.Imput
  N2: Parte2.A1, Parte144.Imput
  N3: Parte2.A2, Parte181.Imput
  N4: Parte2.A3, Parte128.Imput
  N5: Parte2.A4, Parte103.Imput
  N6: Parte2.TX/D1, Parte204.RX-I
  N7: Parte2.RX/D0, Parte204.TX-O
  VCC: Parte2.VCC, Parte103.Vcc, Parte104.Vcc, Parte105.Vcc, Parte106.Vcc, Parte107.Vcc, Parte108.Vcc, Parte109.Vcc, Parte110.Vcc, Parte111.Vcc, Parte112.Vcc, Parte113.Vcc, Parte114.Vcc, Parte115.Vcc, Parte116.Vcc, Parte117.Vcc, Parte118.Vcc, Parte119.Vcc, Parte120.Vcc, Parte121.Vcc, Parte122.Vcc, Parte203.+, Parte204.VCC
  N8: Parte103.Out, Parte104.Imput
  N9: Parte104.Out, Parte105.Imput
  N10: Parte105.Out, Parte106.Imput
  N11: Parte106.Out, Parte107.Imput
  N12: Parte107.Out, Parte108.Imput
  N13: Parte108.Out, Parte112.Imput
  N14: Parte109.Imput, Parte112.Out
  N15: Parte109.Out, Parte110.Imput
  N16: Parte110.Out, Parte111.Imput
  N17: Parte111.Out, Parte120.Imput
  N18: Parte113.Imput, Parte119.Out
  N19: Parte113.Out, Parte121.Imput
  N20: Parte114.Imput, Parte122.Out
  N21: Parte114.Out, Parte119.Imput
  N22: Parte115.Imput, Parte117.Out
  N23: Parte115.Out, Parte116.Imput
  N24: Parte116.Out, Parte122.Imput
  N25: Parte117.Imput, Parte118.Out
  N26: Parte118.Imput, Parte120.Out
  N27: Parte123.Imput, Parte142.Out
  N28: Parte123.Out, Parte139.Imput
  N29: Parte124.Imput, Parte132.Out
  N30: Parte124.Out, Parte125.Imput
  N31: Parte125.Out, Parte133.Imput
  N32: Parte126.Imput, Parte134.Out
  N33: Parte126.Out, Parte135.Imput
  N34: Parte127.Imput, Parte139.Out
  N35: Parte127.Out, Parte131.Imput
  N36: Parte128.Out, Parte130.Imput
  N37: Parte129.Imput, Parte130.Out
  N38: Parte129.Out, Parte134.Imput
  N39: Parte131.Out, Parte138.Imput
  N40: Parte132.Imput, Parte137.Out
  N41: Parte133.Out, Parte142.Imput
  N42: Parte135.Out, Parte136.Imput
  N43: Parte136.Out, Parte137.Imput
  N44: Parte138.Out, Parte140.Imput
  N45: Parte140.Out, Parte141.Imput
  N46: Parte143.Imput, Parte163.Out
  N47: Parte143.Out, Parte149.Imput
  N48: Parte144.Out, Parte162.Imput
  N49: Parte145.Imput, Parte177.Out
  N50: Parte145.Out, Parte174.Imput
  N51: Parte146.Imput, Parte150.Out
  N52: Parte146.Out, Parte170.Imput
  N53: Parte147.Imput, Parte156.Out
  N54: Parte147.Out, Parte161.Imput
  N55: Parte148.Imput, Parte158.Out
  N56: Parte148.Out, Parte166.Imput
  N57: Parte149.Out, Parte175.Imput
  N58: Parte150.Imput, Parte164.Out
  N59: Parte151.Imput, Parte159.Out
  N60: Parte151.Out, Parte178.Imput
  N61: Parte152.Imput, Parte172.Out
  N62: Parte152.Out, Parte157.Imput
  N63: Parte153.Imput, Parte161.Out
  N64: Parte153.Out, Parte176.Imput
  N65: Parte154.Imput, Parte176.Out
  N66: Parte154.Out, Parte171.Imput
  N67: Parte155.Imput, Parte175.Out
  N68: Parte155.Out, Parte169.Imput
  N69: Parte156.Imput, Parte170.Out
  N70: Parte158.Imput, Parte174.Out
  N71: Parte159.Imput, Parte168.Out
  N72: Parte160.Imput, Parte171.Out
  N73: Parte160.Out, Parte172.Imput
  N74: Parte162.Out, Parte165.Imput
  N75: Parte163.Imput, Parte173.Out
  N76: Parte164.Imput, Parte178.Out
  N77: Parte165.Out, Parte177.Imput
  N78: Parte166.Out, Parte173.Imput
  N79: Parte167.Imput, Parte179.Out
  N80: Parte168.Imput, Parte181.Out
  N81: Parte169.Out, Parte180.Imput
  N82: Parte179.Imput, Parte182.Out
  N83: Parte180.Out, Parte182.Imput
  N84: Parte183.Imput, Parte189.Out
  N85: Parte183.Out, Parte202.Imput
  N86: Parte184.Imput, Parte192.Out
  N87: Parte184.Out, Parte194.Imput
  N88: Parte185.Imput, Parte191.Out
  N89: Parte185.Out, Parte197.Imput
  N90: Parte186.Imput, Parte195.Out
  N91: Parte186.Out, Parte187.Imput
  N92: Parte187.Out, Parte196.Imput
  N93: Parte188.Imput, Parte196.Out
  N94: Parte188.Out, Parte191.Imput
  N95: Parte189.Imput, Parte201.Out
  N96: Parte190.Imput, Parte200.Out
  N97: Parte190.Out, Parte199.Imput
  N98: Parte192.Imput, Parte197.Out
  N99: Parte193.Imput, Parte202.Out
  N100: Parte193.Out, Parte195.Imput
  N101: Parte194.Out, Parte200.Imput
  N102: Parte198.Out, Parte201.Imput

custom parts:
  LilyPad Tri-Color LED: Blink any color you need! Use the Tri-Color LED board as a simple indicator, or by pulsing the red, green, and blue channels, you can create any color. Very bright output. This is a common anode design - to turn on a channel you simply need to ground one of the R/G/B pins to illuminate that channel. LilyPad is a wearable technology developed by Leah Buechley and cooperatively designed by Leah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
