# Fritzing sketch CamisaDebianV1 (saved by Fritzing 0.8.3b)
circuit board: 28.2027cm x 33.5026cm

parts:
  Part2 = Lilypad Arduino Board
  Part3 = LilyPad Power Supply
  Part4 = LilyPad LED
  Part5 = LilyPad LED
  Part6 = LilyPad LED
  Part7 = LilyPad LED
  Part8 = LilyPad LED
  Part9 = LilyPad LED
  Part10 = LilyPad LED
  Part11 = LilyPad LED
  Part12 = LilyPad LED
  Part13 = LilyPad LED
  Part14 = LilyPad LED
  Part15 = LilyPad LED
  Part16 = LilyPad LED
  Part17 = LilyPad LED
  Part18 = LilyPad LED
  Part19 = LilyPad LED
  Part20 = LilyPad LED
  Part21 = LilyPad LED
  Part22 = LilyPad LED
  Part23 = LilyPad Button Board
  Part24 = LilyPad LED
  Part25 = LilyPad LED
  Part26 = LilyPad LED
  Part27 = LilyPad LED
  Part28 = LilyPad LED
  Part29 = LilyPad LED
  Part30 = LilyPad LED
  Part31 = LilyPad LED
  Part32 = LilyPad LED
  Part33 = LilyPad LED
  Part34 = LilyPad LED
  Part35 = LilyPad LED
  Part36 = LilyPad LED
  Part37 = LilyPad LED
  Part38 = LilyPad LED
  Part39 = LilyPad LED
  Part40 = LilyPad LED
  Part41 = LilyPad LED
  Part42 = LilyPad LED
  Part43 = LilyPad LED
  Part44 = LilyPad LED
  Part45 = LilyPad LED
  Part46 = LilyPad LED
  Part47 = LilyPad LED

nets:
  GND: Part2.GND, Part3.GND, Part4.-, Part5.-, Part6.-, Part7.-, Part8.-, Part9.-, Part10.-, Part11.-, Part12.-, Part13.-, Part14.-, Part15.-, Part16.-, Part17.-, Part18.-, Part19.-, Part20.-, Part21.-, Part22.-, Part23.-, Part24.-, Part25.-, Part26.-, Part27.-, Part28.-, Part29.-, Part30.-, Part31.-, Part32.-, Part33.-, Part34.-, Part35.-, Part36.-, Part37.-, Part38.-, Part39.-, Part40.-, Part41.-, Part42.-, Part43.-, Part44.-, Part45.-, Part46.-, Part47.-
  N1: Part2.A0, Part5.+, Part38.+
  N2: Part2.A1, Part20.+, Part27.+, Part43.+
  N3: Part2.A2, Part12.+, Part39.+
  N4: Part2.A3, Part19.+, Part28.+, Part44.+
  N5: Part2.A4, Part11.+, Part40.+
  N6: Part2.A5, Part7.+, Part29.+, Part45.+
  N7: Part2.D8, Part10.+
  N8: Part2.D9, Part22.+, Part24.+
  N9: Part2.D10, Part14.+, Part36.+
  N10: Part2.MOSI/D11, Part21.+, Part25.+, Part41.+
  N11: Part2.MISO/D12, Part13.+, Part37.+
  N12: Part2.SCK/D13, Part9.+, Part26.+, Part42.+
  N13: Part2.D6, Part15.+, Part34.+
  N14: Part2.D5, Part16.+, Part33.+
  N15: Part2.D4, Part8.+, Part32.+
  N16: Part2.D3, Part17.+, Part31.+, Part47.+
  N17: Part2.D2, Part23.S
  N18: Part2.TX/D1, Part18.+, Part30.+, Part46.+
  N19: Part2.RX/D0, Part4.+
  N20: Part2.D7, Part6.+, Part35.+
  N21: Part2.VCC, Part3.+
