# Fritzing sketch Electro (saved by Fritzing 0.8.3b)
circuit board: 28.6589cm x 25.7031cm
breadboards: 1

parts:
  Parte2 = LilyPad LED
  Parte3 = LilyPad LED
  Parte5 = LilyPad LED
  Parte6 = LilyPad LED
  Parte8 = LilyPad LED
  Parte9 = LilyPad LED
  Parte10 = LilyPad LED
  Parte11 = LilyPad LED
  Parte13 = LilyPad LED
  Parte14 = LilyPad LED
  Parte15 = LilyPad LED
  Parte16 = LilyPad LED
  Parte17 = LilyPad LED
  Parte19 = LilyPad LED
  Parte21 = LilyPad LED
  Parte22 = LilyPad LED
  Parte24 = LilyPad LED
  Parte25 = LilyPad LED
  Parte26 = LilyPad LED
  Parte28 = LilyPad LED
  Parte29 = LilyPad LED
  Parte30 = LilyPad LED
  Parte31 = LilyPad LED
  Parte32 = LilyPad LED
  Parte33 = LilyPad LED
  Parte34 = LilyPad LED
  Parte35 = LilyPad LED
  Parte36 = LilyPad LED
  Parte37 = LilyPad LED
  Parte40 = LilyPad LED
  Parte41 = LilyPad LED
  Parte42 = LilyPad LED
  Parte43 = LilyPad LED
  Parte44 = LilyPad LED
  Parte46 = LilyPad Button Board
  Parte47 = LilyPad Button Board
  Parte1 = Lilypad Arduino Board
  J1 = female pin header, 2 pins [form="♀ (female)"]
  Parte45 = Lilypad Power Supply

nets:
  N1: Parte2.+, Parte3.+, Parte1.D10
  N2: Parte2.-, Parte3.-, Parte5.-, Parte6.-, Parte8.-, Parte9.-, Parte10.-, Parte11.-, Parte13.-, Parte14.-, Parte15.-, Parte16.-, Parte17.-, Parte19.-, Parte21.-, Parte22.-, Parte24.-, Parte25.-, Parte26.-, Parte28.-, Parte29.-, Parte30.-, Parte31.-, Parte32.-, Parte33.-, Parte34.-, Parte35.-, Parte36.-, Parte37.-, Parte40.-, Parte41.-, Parte42.-, Parte43.-, Parte44.-, Parte46.-, Parte47.-, J1.pin1
  N3: Parte5.+, Parte6.+, Parte1.ISCP_MISO, Parte1.MISO/D12
  N4: Parte8.+, Parte9.+, Parte1.A0
  N5: Parte10.+, Parte11.+, Parte1.ISCP_SCK, Parte1.SCK/D13
  N6: Parte13.+, Parte14.+, Parte1.ISCP_MOSI, Parte1.MOSI/D11
  N7: Parte15.+, Parte16.+, Parte1.D9
  N8: Parte17.+, Parte19.+, Parte1.A1
  N9: Parte21.+, Parte22.+, Parte1.A2
  N10: Parte24.+, Parte25.+, Parte1.A3
  N11: Parte26.+, Parte28.+, Parte1.A4
  N12: Parte29.+, Parte30.+, Parte1.A5
  N13: Parte31.+, Parte32.+, Parte1.RX/D0
  N14: Parte33.+, Parte34.+, Parte1.TX/D1
  N15: Parte35.+, Parte36.+, Parte1.D2
  N16: Parte37.+, Parte44.+, Parte1.D3
  N17: Parte40.+, Parte41.+, Parte1.D8
  N18: Parte42.+, Parte43.+, Parte1.D6
  N19: Parte46.S, Parte1.D5
  N20: Parte47.S, Parte1.D4
  GND: Parte1.GND, Parte45.GND
  N21: Parte1.D7, J1.pin2
  N22: Parte1.VCC, Parte45.+
