# Fritzing sketch PromocionalORISOL (saved by Fritzing 0.8.3b)
circuit board: 9.16994cm x 41.8588cm
circuit board: 9.16994cm x 41.8588cm
breadboards: 1

parts:
  Parte1 = LilyPad Arduino Simple Board
  Parte57 = LilyPad LED
  Parte58 = LilyPad LED
  Parte59 = LilyPad LED
  Parte60 = LilyPad LED
  Parte61 = LilyPad LED
  Parte62 = LilyPad LED
  Parte63 = LilyPad LED
  Parte64 = LilyPad LED
  Parte65 = LilyPad LED
  Parte66 = LilyPad LED
  Parte67 = LilyPad LED
  Parte68 = LilyPad LED
  Parte69 = LilyPad LED
  Parte70 = LilyPad LED
  Parte71 = LilyPad LED
  Parte72 = LilyPad LED
  Parte73 = LilyPad LED
  Parte74 = LilyPad LED
  Parte75 = LilyPad LED
  Parte76 = LilyPad LED
  Parte77 = LilyPad LED
  Parte78 = LilyPad LED
  Parte79 = LilyPad LED
  Parte80 = LilyPad LED
  Parte81 = LilyPad LED
  Parte82 = LilyPad LED
  Parte83 = LilyPad LED
  Parte84 = LilyPad LED
  Parte85 = LilyPad LED
  Parte86 = LilyPad LED
  Parte87 = LilyPad LED
  Parte88 = LilyPad LED
  Parte89 = LilyPad LED
  Parte90 = LilyPad LED
  Parte91 = LilyPad LED
  Parte92 = LilyPad LED
  Parte93 = LilyPad LED
  Parte94 = LilyPad LED
  Parte95 = LilyPad LED
  Parte96 = LilyPad LED
  Parte97 = LilyPad LED
  Parte98 = LilyPad LED
  Parte99 = LilyPad LED
  Parte100 = LilyPad LED
  Parte101 = LilyPad LED
  Parte102 = LilyPad LED
  Parte103 = LilyPad LED
  Parte104 = LilyPad LED
  Parte105 = LilyPad LED
  Parte106 = LilyPad LED
  Parte107 = LilyPad LED
  Parte108 = LilyPad LED
  Parte109 = LilyPad LED
  Parte110 = LilyPad Button Board
  J1 = female pin header, 1 pin [form="♀ (female)"]
  J2 = female pin header, 1 pin [form="♀ (female)"]
  J3 = female pin header, 1 pin [form="♀ (female)"]
  Parte111 = LilyPad LED
  Parte112 = LilyPad LED
  Parte113 = LilyPad LED
  Parte114 = LilyPad LED
  Parte115 = LilyPad LED
  Parte116 = LilyPad LED
  Parte117 = LilyPad LED
  Parte118 = LilyPad LED
  Parte119 = LilyPad LED
  Parte120 = LilyPad LED
  Parte121 = LilyPad LED
  Parte122 = LilyPad LED
  Parte123 = LilyPad LED
  Parte124 = LilyPad LED
  Parte125 = LilyPad LED
  Parte126 = LilyPad LED
  Parte127 = LilyPad LED
  Parte128 = LilyPad LED
  Parte129 = LilyPad LED
  Parte130 = LilyPad LED
  Parte131 = LilyPad LED
  Parte132 = LilyPad LED
  Parte133 = LilyPad LED
  Parte134 = LilyPad LED
  Parte135 = LilyPad LED
  Parte136 = LilyPad LED
  Parte137 = LilyPad LED
  Parte138 = LilyPad LED
  Parte139 = LilyPad LED
  Parte140 = LilyPad LED
  Parte141 = LilyPad LED
  Parte142 = LilyPad LED
  Parte143 = LilyPad LED
  Parte144 = LilyPad LED
  Parte145 = LilyPad LED
  Parte146 = LilyPad LED
  Parte147 = LilyPad LED
  Parte148 = LilyPad LED
  Parte149 = LilyPad LED
  Parte150 = LilyPad LED
  Parte151 = LilyPad LED
  Parte152 = LilyPad LED
  Parte153 = LilyPad LED
  Parte154 = LilyPad LED
  Parte155 = LilyPad LED
  Parte156 = LilyPad LED
  Parte157 = LilyPad LED
  Parte158 = LilyPad LED
  Parte159 = LilyPad LED
  Parte160 = LilyPad LED
  Parte161 = LilyPad LED
  Parte162 = LilyPad LED
  Parte163 = LilyPad LED
  J4 = female pin header, 1 pin [form="♀ (female)"]
  J5 = female pin header, 1 pin [form="♀ (female)"]
  J6 = female pin header, 1 pin [form="♀ (female)"]

nets:
  N1: Parte1.A3, Parte111.-, Parte112.-, Parte113.-, Parte114.-, Parte115.-, Parte116.-, Parte117.-, Parte118.-, Parte119.+, Parte120.-, Parte121.+, Parte122.+, Parte123.+, Parte124.+, Parte125.+, Parte126.+, Parte127.+, Parte128.+, Parte129.+, Parte130.+, Parte131.+, Parte148.+, Parte149.+, Parte150.+, Parte151.+, Parte152.+, Parte153.+, Parte154.+, Parte155.+, Parte156.-, Parte157.-, Parte158.-, Parte159.-, Parte160.-, Parte161.-, Parte162.-, Parte163.-, J4.pin1
  N2: Parte1.A4, Parte111.+, Parte112.+, Parte113.+, Parte114.+, Parte115.+, Parte116.+, Parte117.+, Parte118.+, Parte119.-, Parte120.+, Parte121.-, Parte122.-, Parte123.-, Parte124.-, Parte125.-, Parte126.-, Parte127.-, Parte128.-, Parte129.-, Parte130.-, Parte131.-, Parte132.+, Parte133.+, Parte134.+, Parte135.+, Parte136.+, Parte137.-, Parte138.-, Parte139.-, Parte140.-, Parte141.-, Parte142.-, Parte143.-, Parte144.-, Parte145.-, Parte146.-, Parte147.-, J5.pin1
  N3: Parte1.A5, Parte132.-, Parte133.-, Parte134.-, Parte135.-, Parte136.-, Parte137.+, Parte138.+, Parte139.+, Parte140.+, Parte141.+, Parte142.+, Parte143.+, Parte144.+, Parte145.+, Parte146.+, Parte147.+, Parte148.-, Parte149.-, Parte150.-, Parte151.-, Parte152.-, Parte153.-, Parte154.-, Parte155.-, Parte156.+, Parte157.+, Parte158.+, Parte159.+, Parte160.+, Parte161.+, Parte162.+, Parte163.+, J6.pin1
  N4: Parte1.D6, Parte57.-, Parte58.-, Parte59.-, Parte60.-, Parte61.-, Parte62.-, Parte63.-, Parte64.-, Parte65.+, Parte66.-, Parte67.+, Parte68.+, Parte69.+, Parte70.+, Parte71.+, Parte72.+, Parte73.+, Parte74.+, Parte75.+, Parte76.+, Parte77.+, Parte94.+, Parte95.+, Parte96.+, Parte97.+, Parte98.+, Parte99.+, Parte100.+, Parte101.+, Parte102.-, Parte103.-, Parte104.-, Parte105.-, Parte106.-, Parte107.-, Parte108.-, Parte109.-, J1.pin1
  N5: Parte1.D9, Parte65.-, Parte66.+, Parte67.-, Parte68.-, Parte69.-, Parte70.-, Parte71.-, Parte72.-, Parte73.-, Parte74.-, Parte75.-, Parte76.-, Parte77.-, J2.pin1
  N6: Parte1.D10, Parte78.-, Parte79.-, Parte80.-, Parte81.-, Parte82.-, Parte83.+, Parte84.+, Parte85.+, Parte86.+, Parte87.+, Parte88.+, Parte89.+, Parte90.+, Parte91.+, Parte92.+, Parte93.+, Parte94.-, Parte95.-, Parte96.-, Parte97.-, Parte98.-, Parte99.-, Parte100.-, Parte101.-, Parte102.+, Parte103.+, Parte104.+, Parte105.+, Parte106.+, Parte107.+, Parte108.+, Parte109.+, J3.pin1
  N7: Parte1.D5, Parte110.-
  N8: Parte1.GND, Parte110.S
  N9: Parte57.+, Parte58.+, Parte59.+, Parte60.+, Parte61.+, Parte62.+, Parte63.+, Parte64.+, Parte78.+, Parte79.+, Parte80.+, Parte81.+, Parte82.+, Parte83.-, Parte84.-, Parte85.-, Parte86.-, Parte87.-, Parte88.-, Parte89.-, Parte90.-, Parte91.-, Parte92.-, Parte93.-
