# Fritzing sketch UES (saved by Fritzing 0.8.3b)
circuit board: 36.3981cm x 27.141cm
breadboards: 1

parts:
  Parte4 = Lilypad Power Supply
  Parte6 = LilyPad LED
  Parte7 = LilyPad LED
  Parte8 = LilyPad LED
  Parte9 = LilyPad LED
  Parte10 = LilyPad LED
  Parte11 = LilyPad LED
  Parte12 = LilyPad LED
  Parte13 = LilyPad LED
  Parte14 = LilyPad LED
  Parte15 = LilyPad LED
  Parte16 = LilyPad LED
  Parte17 = LilyPad LED
  Parte18 = LilyPad LED
  Parte19 = LilyPad LED
  Parte20 = LilyPad LED
  Parte21 = LilyPad LED
  Parte22 = LilyPad LED
  Parte24 = LilyPad LED
  Parte25 = LilyPad LED
  Parte26 = LilyPad LED
  Parte27 = LilyPad LED
  Parte28 = LilyPad LED
  Parte29 = LilyPad LED
  Parte30 = LilyPad LED
  Parte31 = LilyPad LED
  Parte1 = Lilypad Arduino Board
  Parte32 = LilyPad LED
  Parte33 = LilyPad Button Board

nets:
  N1: Parte4.+, Parte1.VCC
  GND: Parte4.GND, Parte1.GND, Parte33.-
  N2: Parte6.+, Parte1.D6
  N3: Parte6.-, Parte7.-, Parte8.-, Parte9.-, Parte10.-, Parte11.-, Parte24.-, Parte25.-
  N4: Parte7.+, Parte1.D7
  N5: Parte8.+, Parte1.D8
  N6: Parte9.+, Parte1.SCK/D13
  N7: Parte10.+, Parte1.MISO/D12
  N8: Parte11.+, Parte1.MOSI/D11
  N9: Parte12.+, Parte26.+, Parte27.+, Parte1.A3
  N10: Parte12.-, Parte13.-, Parte14.-, Parte15.-, Parte26.-, Parte27.-, Parte28.-, Parte29.-, Parte30.-, Parte31.-, Parte32.-
  N11: Parte13.+, Parte14.+, Parte1.A0
  N12: Parte15.+, Parte28.+, Parte29.+, Parte1.A1
  N13: Parte16.+, Parte1.D4
  N14: Parte16.-, Parte17.-, Parte18.-, Parte19.-, Parte20.-, Parte21.-, Parte22.-
  N15: Parte17.+, Parte1.A4
  N16: Parte18.+, Parte1.D2
  N17: Parte19.+, Parte1.RX/D0
  N18: Parte20.+, Parte1.D3
  N19: Parte21.+, Parte1.TX/D1
  N20: Parte22.+, Parte1.A5
  N21: Parte24.+, Parte1.D10
  N22: Parte25.+, Parte1.D9
  N23: Parte30.+, Parte31.+, Parte1.A2, Parte32.+
  N24: Parte1.D5, Parte33.S
